// Logisim project 16bit2sadder.circ as structural Verilog: 4 circuits, main circuit main
module main (
  input  in_1,
  input  in_2,
  input  in_3,
  input  in_4,
  input  in_5,
  input  in_6,
  input  in_7,
  input  in_8,
  input  in_9,
  input  in_10,
  input  in_11,
  input  in_12,
  input  in_13,
  input  in_14,
  input  in_15,
  input  in_16,
  input  in_17,
  input  in_18,
  input  in_19,
  input  in_20,
  input  in_21,
  input  in_22,
  input  in_23,
  input  in_24,
  input  in_25,
  input  in_26,
  input  in_27,
  input  in_28,
  input  in_29,
  input  in_30,
  input  in_31,
  input  in_32,
  input  in_33,
  output out_34,
  output out_35,
  output out_36,
  output out_37,
  output out_38,
  output out_39,
  output out_40,
  output out_41,
  output out_42,
  output out_43,
  output out_44,
  output out_45,
  output out_46,
  output out_47,
  output out_48,
  output out_49,
  output out_50
);

  wire n4_bit_adder_2_c_2, n4_bit_adder_3_c_2, n4_bit_adder_4_c_2;

  _4_bit_adder u_4_bit_adder_1 (
    .b4(in_1), .a4(in_2), .b3(in_3), .a3(in_4), .b2(in_5), .a2(in_6), .b1(in_7), .a1(in_8),
    .c(n4_bit_adder_2_c_2), .c_2(out_34), .s4(out_35), .s3(out_36), .s2(out_37), .s1(out_38));
  _4_bit_adder u_4_bit_adder_2 (
    .b4(in_9), .a4(in_10), .b3(in_11), .a3(in_12), .b2(in_13), .a2(in_14), .b1(in_15), .a1(in_16),
    .c(n4_bit_adder_3_c_2), .c_2(n4_bit_adder_2_c_2), .s4(out_39), .s3(out_40), .s2(out_41), .s1(out_42));
  _4_bit_adder u_4_bit_adder_3 (
    .b4(in_17), .a4(in_18), .b3(in_19), .a3(in_20), .b2(in_21), .a2(in_22), .b1(in_23), .a1(in_24),
    .c(n4_bit_adder_4_c_2), .c_2(n4_bit_adder_3_c_2), .s4(out_43), .s3(out_44), .s2(out_45), .s1(out_46));
  _4_bit_adder u_4_bit_adder_4 (
    .b4(in_25), .a4(in_26), .b3(in_27), .a3(in_28), .b2(in_29), .a2(in_30), .b1(in_31), .a1(in_32),
    .c(in_33), .c_2(n4_bit_adder_4_c_2), .s4(out_47), .s3(out_48), .s2(out_49), .s1(out_50));
endmodule

module _4_bit_adder (
  input  b4,
  input  a4,
  input  b3,
  input  a3,
  input  b2,
  input  a2,
  input  b1,
  input  a1,
  input  c,
  output c_2,
  output s4,
  output s3,
  output s2,
  output s1
);

  wire and_1_out, and_2_out, and_3_out, and_4_out, and_5_out, and_6_out, and_7_out, and_8_out, and_9_out,
       and_10_out, and_11_out, or_1_out, or_3_out, or_4_out, xor_1_out, xor_2_out, xor_3_out, xor_4_out,
       xor_5_out, xor_7_out, xor_8_out;

  xor xor_1 (xor_1_out, b4, a4);
  and and_1 (and_1_out, b4, a4);
  xor xor_2 (xor_2_out, b3, a3);
  and and_2 (and_2_out, b3, a3);
  xor xor_3 (xor_3_out, b2, a2);
  and and_3 (and_3_out, b2, a2);
  and and_4 (and_4_out, b1, a1);
  and and_5 (and_5_out, xor_5_out, c);
  or or_1 (or_1_out, and_4_out, and_5_out);
  and and_6 (and_6_out, or_1_out, xor_3_out, xor_2_out, xor_1_out);
  and and_7 (and_7_out, and_3_out, xor_2_out, xor_1_out);
  and and_8 (and_8_out, xor_1_out, and_2_out);
  and and_9 (and_9_out, or_1_out, xor_3_out, xor_2_out);
  and and_10 (and_10_out, xor_2_out, and_3_out);
  and and_11 (and_11_out, or_1_out, xor_3_out);
  or or_2 (c_2, and_6_out, and_7_out, and_8_out, and_1_out);
  or or_3 (or_3_out, and_9_out, and_10_out, and_2_out);
  or or_4 (or_4_out, and_11_out, and_3_out);
  xor xor_4 (xor_4_out, b2, or_1_out);
  xor xor_5 (xor_5_out, b1, a1);
  xor xor_6 (s1, xor_5_out, c);
  xor xor_7 (xor_7_out, b4, or_3_out);
  xor xor_8 (xor_8_out, a3, or_4_out);
  xor xor_9 (s3, xor_8_out, b3);
  xor xor_10 (s2, xor_4_out, a2);
  xor xor_11 (s4, xor_7_out, a4);

  // Notes on the sheet:
  //   p3
  //   g3
  //   p2
  //   g2
  //   p1
  //   g1
  //   c
endmodule

module full_adder (
  input  a,
  input  b,
  input  cin,
  output s,
  output out_5
);

  wire and_1_out, and_2_out, xor_1_out;

  xor xor_1 (xor_1_out, a, b);
  xor xor_2 (s, xor_1_out, cin);
  and and_1 (and_1_out, cin, xor_1_out);
  and and_2 (and_2_out, b, a);
  or or_1 (out_5, and_1_out, and_2_out);
endmodule

module _16bitaddersubtracter (
  input  in_1,
  input  in_2,
  input  in_3,
  input  in_4,
  input  in_5,
  input  in_6,
  input  in_7,
  input  in_8,
  input  in_9,
  input  in_10,
  input  in_11,
  input  in_12,
  input  in_13,
  input  in_14,
  input  in_15,
  input  in_16,
  input  in_17,
  input  in_18,
  input  in_19,
  input  in_20,
  input  in_21,
  input  in_22,
  input  in_23,
  input  in_24,
  input  in_25,
  input  in_26,
  input  in_27,
  input  in_28,
  input  in_29,
  input  in_30,
  input  in_31,
  input  in_32,
  input  in_33,
  output out_34,
  output out_35,
  output out_36,
  output out_37,
  output out_38,
  output out_39,
  output out_40,
  output out_41,
  output out_42,
  output out_43,
  output out_44,
  output out_45,
  output out_46,
  output out_47,
  output out_48,
  output out_49,
  output out_50
);

  wire full_adder_1_out_5, full_adder_2_out_5, full_adder_3_out_5, full_adder_4_out_5, full_adder_5_out_5,
       full_adder_6_out_5, full_adder_7_out_5, full_adder_8_out_5, full_adder_9_out_5, full_adder_10_out_5,
       full_adder_11_out_5, full_adder_12_out_5, full_adder_13_out_5, full_adder_14_out_5,
       full_adder_15_out_5, full_adder_16_out_5, xor_1_out, xor_2_out, xor_3_out, xor_4_out, xor_5_out,
       xor_6_out, xor_7_out, xor_8_out, xor_9_out, xor_10_out, xor_11_out, xor_12_out, xor_13_out,
       xor_14_out, xor_15_out, xor_16_out;

  xor xor_1 (xor_1_out, in_17, in_9);
  full_adder full_adder_1 (.a(in_1), .b(xor_1_out), .cin(in_17), .s(out_34), .out_5(full_adder_1_out_5));
  xor xor_2 (xor_2_out, in_17, in_26);
  full_adder full_adder_2 (.a(in_18), .b(xor_2_out), .cin(full_adder_15_out_5), .s(out_42), .out_5(full_adder_2_out_5));
  xor xor_3 (xor_3_out, in_17, in_10);
  full_adder full_adder_3 (.a(in_2), .b(xor_3_out), .cin(full_adder_1_out_5), .s(out_35), .out_5(full_adder_3_out_5));
  xor xor_4 (xor_4_out, in_17, in_27);
  full_adder full_adder_4 (.a(in_19), .b(xor_4_out), .cin(full_adder_2_out_5), .s(out_43), .out_5(full_adder_4_out_5));
  xor xor_5 (xor_5_out, in_17, in_11);
  xor xor_6 (xor_6_out, in_17, in_28);
  full_adder full_adder_5 (.a(in_3), .b(xor_5_out), .cin(full_adder_3_out_5), .s(out_36), .out_5(full_adder_5_out_5));
  full_adder full_adder_6 (.a(in_20), .b(xor_6_out), .cin(full_adder_4_out_5), .s(out_44), .out_5(full_adder_6_out_5));
  xor xor_7 (xor_7_out, in_17, in_12);
  full_adder full_adder_7 (.a(in_4), .b(xor_7_out), .cin(full_adder_5_out_5), .s(out_37), .out_5(full_adder_7_out_5));
  xor xor_8 (xor_8_out, in_17, in_29);
  full_adder full_adder_8 (.a(in_21), .b(xor_8_out), .cin(full_adder_6_out_5), .s(out_45), .out_5(full_adder_8_out_5));
  xor xor_9 (xor_9_out, in_17, in_13);
  full_adder full_adder_9 (.a(in_5), .b(xor_9_out), .cin(full_adder_7_out_5), .s(out_38), .out_5(full_adder_9_out_5));
  xor xor_10 (xor_10_out, in_17, in_30);
  full_adder full_adder_10 (
    .a(in_22), .b(xor_10_out), .cin(full_adder_8_out_5), .s(out_46), .out_5(full_adder_10_out_5));
  xor xor_11 (xor_11_out, in_17, in_14);
  xor xor_12 (xor_12_out, in_17, in_31);
  full_adder full_adder_11 (
    .a(in_6), .b(xor_11_out), .cin(full_adder_9_out_5), .s(out_39), .out_5(full_adder_11_out_5));
  full_adder full_adder_12 (
    .a(in_23), .b(xor_12_out), .cin(full_adder_10_out_5), .s(out_47), .out_5(full_adder_12_out_5));
  xor xor_13 (xor_13_out, in_17, in_15);
  full_adder full_adder_13 (
    .a(in_7), .b(xor_13_out), .cin(full_adder_11_out_5), .s(out_40), .out_5(full_adder_13_out_5));
  xor xor_14 (xor_14_out, in_17, in_32);
  full_adder full_adder_14 (
    .a(in_24), .b(xor_14_out), .cin(full_adder_12_out_5), .s(out_48), .out_5(full_adder_14_out_5));
  xor xor_15 (xor_15_out, in_17, in_16);
  xor xor_16 (xor_16_out, in_17, in_33);
  full_adder full_adder_15 (
    .a(in_8), .b(xor_15_out), .cin(full_adder_13_out_5), .s(out_41), .out_5(full_adder_15_out_5));
  full_adder full_adder_16 (
    .a(in_25), .b(xor_16_out), .cin(full_adder_14_out_5), .s(out_49), .out_5(full_adder_16_out_5));
  xor xor_17 (out_50, full_adder_16_out_5, full_adder_14_out_5);
endmodule
