// Logisim project 4x1mux.circ as structural Verilog: 1 circuit, main circuit main
module main (
  input  s0,
  input  s1,
  input  d0,
  input  d1,
  input  d2,
  input  d3,
  output \output 
);

  wire and_1_out, and_2_out, and_3_out, and_4_out, not_1_out, not_2_out;

  not not_1 (not_1_out, s0);
  not not_2 (not_2_out, s1);
  and and_1 (and_1_out, not_1_out, not_2_out, d0);
  and and_2 (and_2_out, not_1_out, s1, d1);
  and and_3 (and_3_out, s0, not_2_out, d2);
  and and_4 (and_4_out, s0, s1, d3);
  or or_1 (\output , and_1_out, and_2_out, and_3_out, and_4_out);

  // Notes on the sheet:
  //   4X1 MUX
endmodule
