// Logisim project 8bitnot.circ as structural Verilog: 1 circuit, main circuit main
module main (
  input  xo,
  input  x1,
  input  x2,
  input  x3,
  input  x4,
  input  x5,
  input  x6,
  input  x7,
  output z0,
  output z1,
  output z2,
  output z3,
  output z4,
  output z5,
  output z6,
  output z7
);

  not not_1 (z0, xo);
  not not_2 (z1, x1);
  not not_3 (z2, x2);
  not not_4 (z3, x3);
  not not_5 (z4, x4);
  not not_6 (z5, x5);
  not not_7 (z6, x6);
  not not_8 (z7, x7);

  // Notes on the sheet:
  //   8 bit not logic
endmodule
