// Logisim project 8bitor.circ as structural Verilog: 1 circuit, main circuit main
module main (
  input  xo,
  input  y0,
  input  x1,
  input  y1,
  input  x2,
  input  y2,
  input  x3,
  input  y3,
  input  x4,
  input  y4,
  input  x5,
  input  y5,
  input  x6,
  input  y6,
  input  x7,
  input  y7,
  output z0,
  output z1,
  output z2,
  output z3,
  output z4,
  output z5,
  output z6,
  output z7
);

  or or_1 (z0, xo, y0);
  or or_2 (z1, x1, y1);
  or or_3 (z2, x2, y2);
  or or_4 (z3, x3, y3);
  or or_5 (z4, x4, y4);
  or or_6 (z5, x5, y5);
  or or_7 (z6, x6, y6);
  or or_8 (z7, x7, y7);

  // Notes on the sheet:
  //   8 bit or logic
endmodule
