// Logisim project halfadders.circ as structural Verilog: 1 circuit, main circuit main
module main (
  input  a,
  input  b,
  input  a_2,
  input  b_2,
  output s,
  output c,
  output s_2,
  output c_2
);

  wire nand_1_out, nand_2_out, nand_3_out;

  nand nand_1 (nand_1_out, a_2, b_2);
  nand nand_2 (nand_2_out, a_2, nand_1_out);
  nand nand_3 (nand_3_out, nand_1_out, b_2);
  nand nand_4 (s_2, nand_2_out, nand_3_out);
  xor xor_1 (s, a, b);
  and and_1 (c, b, a);
  nand nand_5 (c_2, nand_1_out, nand_1_out);

  // Notes on the sheet:
  //   hald adder
  //   half adder with nand
endmodule
