// Logisim project question3.circ as structural Verilog: 6 circuits, main circuit main
module main (
  input  x0,
  input  x0_2,
  input  y0,
  input  y0_2,
  input  x1,
  input  x1_2,
  input  y1,
  input  y1_2,
  input  x2,
  input  x2_2,
  input  y2,
  input  y2_2,
  input  x3,
  input  x3_2,
  input  y3,
  input  y3_2,
  input  x4,
  input  x4_2,
  input  y4,
  input  y4_2,
  input  x5,
  input  x5_2,
  input  y5,
  input  y5_2,
  input  x6,
  input  x6_2,
  input  y6,
  input  y6_2,
  input  x7,
  input  in_30,
  input  x7_2,
  input  y7,
  input  in_33,
  input  y7_2,
  input  x0_3,
  input  y0_3,
  input  x1_3,
  input  y1_3,
  input  x0_4,
  input  x2_3,
  input  x1_4,
  input  y2_3,
  input  x2_4,
  input  x3_3,
  input  x3_4,
  input  y3_3,
  input  x4_3,
  input  x4_4,
  input  x5_3,
  input  y4_3,
  input  x6_3,
  input  x5_4,
  input  x7_3,
  input  y5_3,
  input  x6_4,
  input  y6_3,
  input  x7_4,
  input  in_58,
  input  in_59,
  input  y7_3,
  output z0,
  output z0_2,
  output z1,
  output z1_2,
  output z2,
  output z2_2,
  output z3,
  output z3_2,
  output z4,
  output z4_2,
  output z5,
  output z5_2,
  output z6,
  output z6_2,
  output z7,
  output z7_2,
  output z0_3,
  output z0_4,
  output z1_3,
  output z1_4,
  output z2_3,
  output z2_4,
  output z3_3,
  output z3_4,
  output z4_3,
  output z4_4,
  output z5_3,
  output z5_4,
  output z6_3,
  output z6_4,
  output z7_3,
  output z7_4
);

  wire n8bit_and_1_z0, n8bit_and_1_z1, n8bit_and_1_z2, n8bit_and_1_z3, n8bit_and_1_z4, n8bit_and_1_z5,
       n8bit_and_1_z6, n8bit_and_1_z7, n8bit_not_1_z0, n8bit_not_1_z1, n8bit_not_1_z2, n8bit_not_1_z3,
       n8bit_not_1_z4, n8bit_not_1_z5, n8bit_not_1_z6, n8bit_not_1_z7, n8bit_or_1_z0, n8bit_or_1_z1,
       n8bit_or_1_z2, n8bit_or_1_z3, n8bit_or_1_z4, n8bit_or_1_z5, n8bit_or_1_z6, n8bit_or_1_z7,
       n8bit_xor_1_z0, n8bit_xor_1_z1, n8bit_xor_1_z2, n8bit_xor_1_z3, n8bit_xor_1_z4, n8bit_xor_1_z5,
       n8bit_xor_1_z6, n8bit_xor_1_z7;

  _8bit_and u_8bit_and_1 (
    .xo(x0), .y0(y0), .x1(x1), .y1(y1), .x2(x2), .y2(y2), .x3(x3), .y3(y3), .x4(x4), .y4(y4), .x5(x5),
    .y5(y5), .x6(x6), .y6(y6), .x7(x7), .y7(y7), .z0(n8bit_and_1_z0), .z1(n8bit_and_1_z1),
    .z2(n8bit_and_1_z2), .z3(n8bit_and_1_z3), .z4(n8bit_and_1_z4), .z5(n8bit_and_1_z5), .z6(n8bit_and_1_z6),
    .z7(n8bit_and_1_z7));
  _8bit_or u_8bit_or_1 (
    .xo(x0_3), .y0(y0_3), .x1(x1_3), .y1(y1_3), .x2(x2_3), .y2(y2_3), .x3(x3_3), .y3(y3_3), .x4(x4_4),
    .y4(y4_3), .x5(x5_4), .y5(y5_3), .x6(x6_4), .y6(y6_3), .x7(x7_4), .y7(y7_3), .z0(n8bit_or_1_z0),
    .z1(n8bit_or_1_z1), .z2(n8bit_or_1_z2), .z3(n8bit_or_1_z3), .z4(n8bit_or_1_z4), .z5(n8bit_or_1_z5),
    .z6(n8bit_or_1_z6), .z7(n8bit_or_1_z7));
  assign z0 = in_30 ? n8bit_and_1_z0 : 1'bz;  // Controlled_Buffer controlled_buffer_1
  assign z1 = in_30 ? n8bit_and_1_z1 : 1'bz;  // Controlled_Buffer controlled_buffer_2
  assign z2 = in_30 ? n8bit_and_1_z2 : 1'bz;  // Controlled_Buffer controlled_buffer_3
  assign z3 = in_30 ? n8bit_and_1_z3 : 1'bz;  // Controlled_Buffer controlled_buffer_4
  assign z4 = in_30 ? n8bit_and_1_z4 : 1'bz;  // Controlled_Buffer controlled_buffer_5
  assign z5 = in_30 ? n8bit_and_1_z5 : 1'bz;  // Controlled_Buffer controlled_buffer_6
  assign z6 = in_30 ? n8bit_and_1_z6 : 1'bz;  // Controlled_Buffer controlled_buffer_7
  assign z7 = in_30 ? n8bit_and_1_z7 : 1'bz;  // Controlled_Buffer controlled_buffer_8
  assign z0_3 = in_58 ? n8bit_or_1_z0 : 1'bz;  // Controlled_Buffer controlled_buffer_9
  assign z1_3 = in_58 ? n8bit_or_1_z1 : 1'bz;  // Controlled_Buffer controlled_buffer_10
  assign z2_3 = in_58 ? n8bit_or_1_z2 : 1'bz;  // Controlled_Buffer controlled_buffer_11
  assign z3_3 = in_58 ? n8bit_or_1_z3 : 1'bz;  // Controlled_Buffer controlled_buffer_12
  assign z4_3 = in_58 ? n8bit_or_1_z4 : 1'bz;  // Controlled_Buffer controlled_buffer_13
  assign z5_3 = in_58 ? n8bit_or_1_z5 : 1'bz;  // Controlled_Buffer controlled_buffer_14
  assign z6_3 = in_58 ? n8bit_or_1_z6 : 1'bz;  // Controlled_Buffer controlled_buffer_15
  assign z7_3 = in_58 ? n8bit_or_1_z7 : 1'bz;  // Controlled_Buffer controlled_buffer_16
  _8bit_xor u_8bit_xor_1 (
    .xo(x0_2), .y0(y0_2), .x1(x1_2), .y1(y1_2), .x2(x2_2), .y2(y2_2), .x3(x3_2), .y3(y3_2), .x4(x4_2),
    .y4(y4_2), .x5(x5_2), .y5(y5_2), .x6(x6_2), .y6(y6_2), .x7(x7_2), .y7(y7_2), .z0(n8bit_xor_1_z0),
    .z1(n8bit_xor_1_z1), .z2(n8bit_xor_1_z2), .z3(n8bit_xor_1_z3), .z4(n8bit_xor_1_z4), .z5(n8bit_xor_1_z5),
    .z6(n8bit_xor_1_z6), .z7(n8bit_xor_1_z7));
  _8bit_not u_8bit_not_1 (
    .xo(x0_4), .x1(x1_4), .x2(x2_4), .x3(x3_4), .x4(x4_3), .x5(x5_3), .x6(x6_3), .x7(x7_3),
    .z0(n8bit_not_1_z0), .z1(n8bit_not_1_z1), .z2(n8bit_not_1_z2), .z3(n8bit_not_1_z3), .z4(n8bit_not_1_z4),
    .z5(n8bit_not_1_z5), .z6(n8bit_not_1_z6), .z7(n8bit_not_1_z7));
  assign z0_2 = in_33 ? n8bit_xor_1_z0 : 1'bz;  // Controlled_Buffer controlled_buffer_17
  assign z1_2 = in_33 ? n8bit_xor_1_z1 : 1'bz;  // Controlled_Buffer controlled_buffer_18
  assign z2_2 = in_33 ? n8bit_xor_1_z2 : 1'bz;  // Controlled_Buffer controlled_buffer_19
  assign z3_2 = in_33 ? n8bit_xor_1_z3 : 1'bz;  // Controlled_Buffer controlled_buffer_20
  assign z4_2 = in_33 ? n8bit_xor_1_z4 : 1'bz;  // Controlled_Buffer controlled_buffer_21
  assign z5_2 = in_33 ? n8bit_xor_1_z5 : 1'bz;  // Controlled_Buffer controlled_buffer_22
  assign z6_2 = in_33 ? n8bit_xor_1_z6 : 1'bz;  // Controlled_Buffer controlled_buffer_23
  assign z7_2 = in_33 ? n8bit_xor_1_z7 : 1'bz;  // Controlled_Buffer controlled_buffer_24
  assign z0_4 = in_59 ? n8bit_not_1_z0 : 1'bz;  // Controlled_Buffer controlled_buffer_25
  assign z1_4 = in_59 ? n8bit_not_1_z1 : 1'bz;  // Controlled_Buffer controlled_buffer_26
  assign z2_4 = in_59 ? n8bit_not_1_z2 : 1'bz;  // Controlled_Buffer controlled_buffer_27
  assign z3_4 = in_59 ? n8bit_not_1_z3 : 1'bz;  // Controlled_Buffer controlled_buffer_28
  assign z4_4 = in_59 ? n8bit_not_1_z4 : 1'bz;  // Controlled_Buffer controlled_buffer_29
  assign z5_4 = in_59 ? n8bit_not_1_z5 : 1'bz;  // Controlled_Buffer controlled_buffer_30
  assign z6_4 = in_59 ? n8bit_not_1_z6 : 1'bz;  // Controlled_Buffer controlled_buffer_31
  assign z7_4 = in_59 ? n8bit_not_1_z7 : 1'bz;  // Controlled_Buffer controlled_buffer_32

  // Notes on the sheet:
  //   8bit or with tristate
  //   8bit and with tristate logic
  //   8bit not with tristate
  //   8 bit xor with tristate
endmodule

module _8bit_and (
  input  xo,
  input  y0,
  input  x1,
  input  y1,
  input  x2,
  input  y2,
  input  x3,
  input  y3,
  input  x4,
  input  y4,
  input  x5,
  input  y5,
  input  x6,
  input  y6,
  input  x7,
  input  y7,
  output z0,
  output z1,
  output z2,
  output z3,
  output z4,
  output z5,
  output z6,
  output z7
);

  and and_1 (z0, xo, y0);
  and and_2 (z1, x1, y1);
  and and_3 (z2, x2, y2);
  and and_4 (z3, x3, y3);
  and and_5 (z4, x4, y4);
  and and_6 (z5, x5, y5);
  and and_7 (z6, x6, y6);
  and and_8 (z7, x7, y7);

  // Notes on the sheet:
  //   8 bit and logic
endmodule

module _8bit_or (
  input  xo,
  input  y0,
  input  x1,
  input  y1,
  input  x2,
  input  y2,
  input  x3,
  input  y3,
  input  x4,
  input  y4,
  input  x5,
  input  y5,
  input  x6,
  input  y6,
  input  x7,
  input  y7,
  output z0,
  output z1,
  output z2,
  output z3,
  output z4,
  output z5,
  output z6,
  output z7
);

  or or_1 (z0, xo, y0);
  or or_2 (z1, x1, y1);
  or or_3 (z2, x2, y2);
  or or_4 (z3, x3, y3);
  or or_5 (z4, x4, y4);
  or or_6 (z5, x5, y5);
  or or_7 (z6, x6, y6);
  or or_8 (z7, x7, y7);

  // Notes on the sheet:
  //   8 bit or logic
endmodule

module _8bit_not (
  input  xo,
  input  x1,
  input  x2,
  input  x3,
  input  x4,
  input  x5,
  input  x6,
  input  x7,
  output z0,
  output z1,
  output z2,
  output z3,
  output z4,
  output z5,
  output z6,
  output z7
);

  not not_1 (z0, xo);
  not not_2 (z1, x1);
  not not_3 (z2, x2);
  not not_4 (z3, x3);
  not not_5 (z4, x4);
  not not_6 (z5, x5);
  not not_7 (z6, x6);
  not not_8 (z7, x7);

  // Notes on the sheet:
  //   8 bit not logic
endmodule

module _8bit_xor (
  input  xo,
  input  y0,
  input  x1,
  input  y1,
  input  x2,
  input  y2,
  input  x3,
  input  y3,
  input  x4,
  input  y4,
  input  x5,
  input  y5,
  input  x6,
  input  y6,
  input  x7,
  input  y7,
  output z0,
  output z1,
  output z2,
  output z3,
  output z4,
  output z5,
  output z6,
  output z7
);

  xor xor_1 (z0, xo, y0);
  xor xor_2 (z1, x1, y1);
  xor xor_3 (z2, x2, y2);
  xor xor_4 (z3, x3, y3);
  xor xor_5 (z4, x4, y4);
  xor xor_6 (z5, x5, y5);
  xor xor_7 (z6, x6, y6);
  xor xor_8 (z7, x7, y7);

  // Notes on the sheet:
  //   8 bit xor logic
endmodule

module all (
  input  xo,
  input  xo_2,
  input  y0,
  input  xo_3,
  input  y0_2,
  input  y0_3,
  input  x1,
  input  x1_2,
  input  xo_4,
  input  y1,
  input  x1_3,
  input  y1_2,
  input  y1_3,
  input  x1_4,
  input  x2,
  input  x2_2,
  input  y2,
  input  x2_3,
  input  y2_2,
  input  x2_4,
  input  y2_3,
  input  x3,
  input  x3_2,
  input  y3,
  input  x3_3,
  input  x3_4,
  input  y3_2,
  input  y3_3,
  input  x4,
  input  x4_2,
  input  x4_3,
  input  y4,
  input  x4_4,
  input  y4_2,
  input  x5,
  input  y4_3,
  input  x5_2,
  input  x5_3,
  input  y5,
  input  x5_4,
  input  x6,
  input  y5_2,
  input  y5_3,
  input  x6_2,
  input  x7,
  input  x6_3,
  input  y6,
  input  x6_4,
  input  y6_2,
  input  y6_3,
  input  in_51,
  input  x7_2,
  input  x7_3,
  input  y7,
  input  x7_4,
  input  y7_2,
  input  in_57,
  input  y7_3,
  input  in_59,
  input  in_60,
  output z0,
  output z0_2,
  output z0_3,
  output z1,
  output z0_4,
  output z1_2,
  output z1_3,
  output z0_5,
  output z2,
  output z2_2,
  output z2_3,
  output z0_6,
  output z3,
  output z3_2,
  output z0_7,
  output z3_3,
  output z0_8,
  output z4,
  output z4_2,
  output z4_3,
  output z0_9,
  output z5,
  output z5_2,
  output z0_10,
  output z5_3,
  output z0_11,
  output z6,
  output z6_2,
  output z6_3,
  output z7,
  output z7_2,
  output z7_3
);

  wire and_1_out, and_2_out, and_3_out, and_4_out, and_5_out, and_6_out, and_7_out, and_8_out, not_1_out,
       not_2_out, not_3_out, not_4_out, not_5_out, not_6_out, not_7_out, not_8_out, or_1_out, or_2_out,
       or_3_out, or_4_out, or_5_out, or_6_out, or_7_out, or_8_out, xor_1_out, xor_2_out, xor_3_out,
       xor_4_out, xor_5_out, xor_6_out, xor_7_out, xor_8_out;

  and and_1 (and_1_out, xo, y0);
  and and_2 (and_2_out, x1, y1);
  and and_3 (and_3_out, x2, y2);
  and and_4 (and_4_out, x3, y3);
  and and_5 (and_5_out, x4, y4);
  and and_6 (and_6_out, x5_2, y5);
  and and_7 (and_7_out, x6_2, y6);
  and and_8 (and_8_out, x7_2, y7);
  assign z0 = in_57 ? and_1_out : 1'bz;  // Controlled_Buffer controlled_buffer_1
  assign z1 = in_57 ? and_2_out : 1'bz;  // Controlled_Buffer controlled_buffer_2
  assign z2 = in_57 ? and_3_out : 1'bz;  // Controlled_Buffer controlled_buffer_3
  assign z3 = in_57 ? and_4_out : 1'bz;  // Controlled_Buffer controlled_buffer_4
  assign z4 = in_57 ? and_5_out : 1'bz;  // Controlled_Buffer controlled_buffer_5
  assign z5 = in_57 ? and_6_out : 1'bz;  // Controlled_Buffer controlled_buffer_6
  assign z6 = in_57 ? and_7_out : 1'bz;  // Controlled_Buffer controlled_buffer_7
  assign z7 = in_57 ? and_8_out : 1'bz;  // Controlled_Buffer controlled_buffer_8
  or or_1 (or_1_out, xo_2, y0_2);
  or or_2 (or_2_out, x1_2, y1_2);
  or or_3 (or_3_out, x2_2, y2_2);
  or or_4 (or_4_out, x3_2, y3_2);
  or or_5 (or_5_out, x4_3, y4_2);
  or or_6 (or_6_out, x5_3, y5_2);
  or or_7 (or_7_out, x6_3, y6_2);
  or or_8 (or_8_out, x7_3, y7_2);
  assign z0_2 = in_59 ? or_1_out : 1'bz;  // Controlled_Buffer controlled_buffer_9
  assign z1_2 = in_59 ? or_2_out : 1'bz;  // Controlled_Buffer controlled_buffer_10
  assign z2_2 = in_59 ? or_3_out : 1'bz;  // Controlled_Buffer controlled_buffer_11
  assign z3_2 = in_59 ? or_4_out : 1'bz;  // Controlled_Buffer controlled_buffer_12
  assign z4_2 = in_59 ? or_5_out : 1'bz;  // Controlled_Buffer controlled_buffer_13
  assign z5_2 = in_59 ? or_6_out : 1'bz;  // Controlled_Buffer controlled_buffer_14
  assign z6_2 = in_59 ? or_7_out : 1'bz;  // Controlled_Buffer controlled_buffer_15
  assign z7_2 = in_59 ? or_8_out : 1'bz;  // Controlled_Buffer controlled_buffer_16
  xor xor_1 (xor_1_out, xo_3, y0_3);
  xor xor_2 (xor_2_out, x1_3, y1_3);
  xor xor_3 (xor_3_out, x2_3, y2_3);
  xor xor_4 (xor_4_out, x3_3, y3_3);
  xor xor_5 (xor_5_out, x4_4, y4_3);
  xor xor_6 (xor_6_out, x5_4, y5_3);
  xor xor_7 (xor_7_out, x6_4, y6_3);
  xor xor_8 (xor_8_out, x7_4, y7_3);
  assign z0_3 = in_60 ? xor_1_out : 1'bz;  // Controlled_Buffer controlled_buffer_17
  assign z1_3 = in_60 ? xor_2_out : 1'bz;  // Controlled_Buffer controlled_buffer_18
  assign z2_3 = in_60 ? xor_3_out : 1'bz;  // Controlled_Buffer controlled_buffer_19
  assign z3_3 = in_60 ? xor_4_out : 1'bz;  // Controlled_Buffer controlled_buffer_20
  assign z4_3 = in_60 ? xor_5_out : 1'bz;  // Controlled_Buffer controlled_buffer_21
  assign z5_3 = in_60 ? xor_6_out : 1'bz;  // Controlled_Buffer controlled_buffer_22
  assign z6_3 = in_60 ? xor_7_out : 1'bz;  // Controlled_Buffer controlled_buffer_23
  assign z7_3 = in_60 ? xor_8_out : 1'bz;  // Controlled_Buffer controlled_buffer_24
  not not_1 (not_1_out, xo_4);
  not not_2 (not_2_out, x1_4);
  not not_3 (not_3_out, x2_4);
  not not_4 (not_4_out, x3_4);
  not not_5 (not_5_out, x4_2);
  not not_6 (not_6_out, x5);
  not not_7 (not_7_out, x6);
  not not_8 (not_8_out, x7);
  assign z0_4 = in_51 ? not_1_out : 1'bz;  // Controlled_Buffer controlled_buffer_25
  assign z0_5 = in_51 ? not_2_out : 1'bz;  // Controlled_Buffer controlled_buffer_26
  assign z0_6 = in_51 ? not_3_out : 1'bz;  // Controlled_Buffer controlled_buffer_27
  assign z0_7 = in_51 ? not_4_out : 1'bz;  // Controlled_Buffer controlled_buffer_28
  assign z0_8 = in_51 ? not_5_out : 1'bz;  // Controlled_Buffer controlled_buffer_29
  assign z0_9 = in_51 ? not_6_out : 1'bz;  // Controlled_Buffer controlled_buffer_30
  assign z0_10 = in_51 ? not_7_out : 1'bz;  // Controlled_Buffer controlled_buffer_31
  assign z0_11 = in_51 ? not_8_out : 1'bz;  // Controlled_Buffer controlled_buffer_32

  // Notes on the sheet:
  //   8 bit and tristate
  //   8 bit or tristate
  //   8 bit xor tristate
  //   8 bit not tristate
endmodule
