// Logisim project question5.circ as structural Verilog: 9 circuits, main circuit main
module main (
  input  x0,
  input  y0,
  input  x1,
  input  y1,
  input  x2,
  input  y2,
  input  x3,
  input  y3,
  input  x4,
  input  y4,
  input  x5,
  input  y5,
  input  x6,
  input  y6,
  input  x7,
  input  y7,
  input  z,
  input  s1,
  input  s2,
  output out_20,
  output out_21,
  output out_22,
  output out_23,
  output out_24,
  output out_25,
  output out_26,
  output out_27
);

  wire and_1_out, and_2_out, and_3_out, and_4_out, and_5_out, and_6_out, and_7_out, and_8_out, and_9_out,
       and_10_out, and_11_out, and_12_out, and_13_out, and_14_out, and_15_out, and_16_out, and_17_out,
       and_18_out, and_19_out, and_20_out, and_21_out, and_22_out, and_23_out, and_24_out, and_25_out,
       and_26_out, and_27_out, and_28_out, and_29_out, and_30_out, and_31_out, and_32_out,
       andwithtristate_1_z0, andwithtristate_1_z1, andwithtristate_1_z2, andwithtristate_1_z3,
       andwithtristate_1_z4, andwithtristate_1_z5, andwithtristate_1_z6, andwithtristate_1_z7, not_1_out,
       not_2_out, notwithtri_1_z0, notwithtri_1_z1, notwithtri_1_z2, notwithtri_1_z3, notwithtri_1_z4,
       notwithtri_1_z5, notwithtri_1_z6, notwithtri_1_z7, orwithtri_1_z0, orwithtri_1_z1, orwithtri_1_z2,
       orwithtri_1_z3, orwithtri_1_z4, orwithtri_1_z5, orwithtri_1_z6, orwithtri_1_z7, xorwithtri_1_z0,
       xorwithtri_1_z1, xorwithtri_1_z2, xorwithtri_1_z3, xorwithtri_1_z4, xorwithtri_1_z5, xorwithtri_1_z6,
       xorwithtri_1_z7;

  andwithtristate andwithtristate_1 (
    .x0(x0), .y0(y0), .x1(x1), .y1(y1), .x2(x2), .y2(y2), .x3(x3), .y3(y3), .x4(x4), .y4(y4), .x5(x5),
    .y5(y5), .x6(x6), .y6(y6), .x7(x7), .y7(y7), .z(z), .z0(andwithtristate_1_z0), .z1(andwithtristate_1_z1),
    .z2(andwithtristate_1_z2), .z3(andwithtristate_1_z3), .z4(andwithtristate_1_z4),
    .z5(andwithtristate_1_z5), .z6(andwithtristate_1_z6), .z7(andwithtristate_1_z7));
  orwithtri orwithtri_1 (
    .x0(x0), .y0(y0), .x1(x1), .y1(y1), .x2(x2), .y2(y2), .x3(x3), .y3(y3), .x4(x4), .y4(y4), .x5(x5),
    .y5(y5), .x6(x6), .y6(y6), .x7(x7), .y7(y7), .in_16(z), .z0(orwithtri_1_z0), .z1(orwithtri_1_z1),
    .z2(orwithtri_1_z2), .z3(orwithtri_1_z3), .z4(orwithtri_1_z4), .z5(orwithtri_1_z5), .z6(orwithtri_1_z6),
    .z7(orwithtri_1_z7));
  notwithtri notwithtri_1 (
    .x0(x0), .x1(x1), .x2(x2), .x3(x3), .x4(x4), .x5(x5), .x6(x6), .x7(x7), .in_9(z), .z0(notwithtri_1_z0),
    .z1(notwithtri_1_z1), .z2(notwithtri_1_z2), .z3(notwithtri_1_z3), .z4(notwithtri_1_z4),
    .z5(notwithtri_1_z5), .z6(notwithtri_1_z6), .z7(notwithtri_1_z7));
  not not_1 (not_1_out, s1);
  not not_2 (not_2_out, s2);
  xorwithtri xorwithtri_1 (
    .x0(x0), .y0(y0), .x1(x1), .y1(y1), .x2(x2), .y2(y2), .x3(x3), .y3(y3), .x4(x4), .y4(y4), .x5(x5),
    .y5(y5), .x6(x6), .y6(y6), .x7(x7), .y7(y7), .in_16(z), .z0(xorwithtri_1_z0), .z1(xorwithtri_1_z1),
    .z2(xorwithtri_1_z2), .z3(xorwithtri_1_z3), .z4(xorwithtri_1_z4), .z5(xorwithtri_1_z5),
    .z6(xorwithtri_1_z6), .z7(xorwithtri_1_z7));
  and and_1 (and_1_out, not_1_out, not_2_out, andwithtristate_1_z0);
  and and_2 (and_2_out, not_1_out, andwithtristate_1_z1, not_2_out);
  and and_3 (and_3_out, not_1_out, andwithtristate_1_z2, not_2_out);
  and and_4 (and_4_out, not_1_out, andwithtristate_1_z3, not_2_out);
  and and_5 (and_5_out, not_1_out, andwithtristate_1_z4, not_2_out);
  and and_6 (and_6_out, not_1_out, not_2_out, andwithtristate_1_z5);
  and and_7 (and_7_out, not_1_out, not_2_out, andwithtristate_1_z6);
  and and_8 (and_8_out, andwithtristate_1_z7, not_1_out, not_2_out);
  and and_9 (and_9_out, s1, not_2_out, orwithtri_1_z0);
  and and_10 (and_10_out, not_2_out, orwithtri_1_z1, s1);
  and and_11 (and_11_out, not_2_out, orwithtri_1_z2, s1);
  and and_12 (and_12_out, not_2_out, orwithtri_1_z3, s1);
  and and_13 (and_13_out, not_2_out, orwithtri_1_z4, s1);
  and and_14 (and_14_out, not_2_out, s1, orwithtri_1_z5);
  and and_15 (and_15_out, not_2_out, s1, orwithtri_1_z6);
  and and_16 (and_16_out, orwithtri_1_z7, not_2_out, s1);
  and and_17 (and_17_out, s2, not_1_out, xorwithtri_1_z0);
  and and_18 (and_18_out, not_1_out, xorwithtri_1_z1, s2);
  and and_19 (and_19_out, not_1_out, xorwithtri_1_z2, s2);
  and and_20 (and_20_out, not_1_out, xorwithtri_1_z3, s2);
  and and_21 (and_21_out, not_1_out, xorwithtri_1_z4, s2);
  and and_22 (and_22_out, not_1_out, s2, xorwithtri_1_z5);
  and and_23 (and_23_out, not_1_out, s2, xorwithtri_1_z6);
  and and_24 (and_24_out, xorwithtri_1_z7, not_1_out, s2);
  and and_25 (and_25_out, notwithtri_1_z0, s2, s1);
  and and_26 (and_26_out, notwithtri_1_z1, s1, s2);
  and and_27 (and_27_out, notwithtri_1_z2, s2, s1);
  and and_28 (and_28_out, notwithtri_1_z3, s2, s1);
  and and_29 (and_29_out, notwithtri_1_z4, s2, s1);
  and and_30 (and_30_out, notwithtri_1_z5, s2, s1);
  and and_31 (and_31_out, notwithtri_1_z6, s2, s1);
  and and_32 (and_32_out, notwithtri_1_z7, s2, s1);
  or or_1 (out_20, and_1_out, and_9_out, and_17_out, and_25_out);
  or or_2 (out_21, and_2_out, and_10_out, and_18_out, and_26_out);
  or or_3 (out_22, and_3_out, and_11_out, and_19_out, and_27_out);
  or or_4 (out_23, and_4_out, and_12_out, and_20_out, and_28_out);
  or or_5 (out_24, and_5_out, and_13_out, and_21_out, and_29_out);
  or or_6 (out_25, and_6_out, and_14_out, and_22_out, and_30_out);
  or or_7 (out_26, and_7_out, and_15_out, and_23_out, and_31_out);
  or or_8 (out_27, and_8_out, and_16_out, and_24_out, and_32_out);

  // Notes on the sheet:
  //   not consides x as input only
  //   1-0 0r
  //   0-0 and
  //   and 00
  //   or 01
  //   not 11
  //   xor 10
endmodule

module \and  (
  input  xo,
  input  y0,
  input  x1,
  input  y1,
  input  x2,
  input  y2,
  input  x3,
  input  y3,
  input  x4,
  input  y4,
  input  x5,
  input  y5,
  input  x6,
  input  y6,
  input  x7,
  input  y7,
  output z0,
  output z1,
  output z2,
  output z3,
  output z4,
  output z5,
  output z6,
  output z7
);

  and and_1 (z0, xo, y0);
  and and_2 (z1, x1, y1);
  and and_3 (z2, x2, y2);
  and and_4 (z3, x3, y3);
  and and_5 (z4, x4, y4);
  and and_6 (z5, x5, y5);
  and and_7 (z6, x6, y6);
  and and_8 (z7, x7, y7);

  // Notes on the sheet:
  //   8 bit and logic
endmodule

module \or  (
  input  xo,
  input  y0,
  input  x1,
  input  y1,
  input  x2,
  input  y2,
  input  x3,
  input  y3,
  input  x4,
  input  y4,
  input  x5,
  input  y5,
  input  x6,
  input  y6,
  input  x7,
  input  y7,
  output z0,
  output z1,
  output z2,
  output z3,
  output z4,
  output z5,
  output z6,
  output z7
);

  or or_1 (z0, xo, y0);
  or or_2 (z1, x1, y1);
  or or_3 (z2, x2, y2);
  or or_4 (z3, x3, y3);
  or or_5 (z4, x4, y4);
  or or_6 (z5, x5, y5);
  or or_7 (z6, x6, y6);
  or or_8 (z7, x7, y7);

  // Notes on the sheet:
  //   8 bit or logic
endmodule

module \xor  (
  input  xo,
  input  y0,
  input  x1,
  input  y1,
  input  x2,
  input  y2,
  input  x3,
  input  y3,
  input  x4,
  input  y4,
  input  x5,
  input  y5,
  input  x6,
  input  y6,
  input  x7,
  input  y7,
  output z0,
  output z1,
  output z2,
  output z3,
  output z4,
  output z5,
  output z6,
  output z7
);

  xor xor_1 (z0, xo, y0);
  xor xor_2 (z1, x1, y1);
  xor xor_3 (z2, x2, y2);
  xor xor_4 (z3, x3, y3);
  xor xor_5 (z4, x4, y4);
  xor xor_6 (z5, x5, y5);
  xor xor_7 (z6, x6, y6);
  xor xor_8 (z7, x7, y7);

  // Notes on the sheet:
  //   8 bit or logic
endmodule

module \not  (
  input  xo,
  input  x1,
  input  x2,
  input  x3,
  input  x4,
  input  x5,
  input  x6,
  input  x7,
  output z0,
  output z1,
  output z2,
  output z3,
  output z4,
  output z5,
  output z6,
  output z7
);

  not not_1 (z0, xo);
  not not_2 (z1, x1);
  not not_3 (z2, x2);
  not not_4 (z3, x3);
  not not_5 (z4, x4);
  not not_6 (z5, x5);
  not not_7 (z6, x6);
  not not_8 (z7, x7);

  // Notes on the sheet:
  //   8 bit not logic
endmodule

module andwithtristate (
  input  x0,
  input  y0,
  input  x1,
  input  y1,
  input  x2,
  input  y2,
  input  x3,
  input  y3,
  input  x4,
  input  y4,
  input  x5,
  input  y5,
  input  x6,
  input  y6,
  input  x7,
  input  z,
  input  y7,
  output z0,
  output z1,
  output z2,
  output z3,
  output z4,
  output z5,
  output z6,
  output z7
);

  wire and_1_z0, and_1_z1, and_1_z2, and_1_z3, and_1_z4, and_1_z5, and_1_z6, and_1_z7;

  \and  and_1 (
    .xo(x0), .y0(y0), .x1(x1), .y1(y1), .x2(x2), .y2(y2), .x3(x3), .y3(y3), .x4(x4), .y4(y4), .x5(x5),
    .y5(y5), .x6(x6), .y6(y6), .x7(x7), .y7(y7), .z0(and_1_z0), .z1(and_1_z1), .z2(and_1_z2), .z3(and_1_z3),
    .z4(and_1_z4), .z5(and_1_z5), .z6(and_1_z6), .z7(and_1_z7));
  assign z0 = z ? and_1_z0 : 1'bz;  // Controlled_Buffer controlled_buffer_1
  assign z1 = z ? and_1_z1 : 1'bz;  // Controlled_Buffer controlled_buffer_2
  assign z2 = z ? and_1_z2 : 1'bz;  // Controlled_Buffer controlled_buffer_3
  assign z3 = z ? and_1_z3 : 1'bz;  // Controlled_Buffer controlled_buffer_4
  assign z4 = z ? and_1_z4 : 1'bz;  // Controlled_Buffer controlled_buffer_5
  assign z5 = z ? and_1_z5 : 1'bz;  // Controlled_Buffer controlled_buffer_6
  assign z6 = z ? and_1_z6 : 1'bz;  // Controlled_Buffer controlled_buffer_7
  assign z7 = z ? and_1_z7 : 1'bz;  // Controlled_Buffer controlled_buffer_8
endmodule

module orwithtri (
  input  x0,
  input  y0,
  input  x1,
  input  y1,
  input  x2,
  input  y2,
  input  x3,
  input  y3,
  input  x4,
  input  y4,
  input  x5,
  input  y5,
  input  x6,
  input  y6,
  input  x7,
  input  in_16,
  input  y7,
  output z0,
  output z1,
  output z2,
  output z3,
  output z4,
  output z5,
  output z6,
  output z7
);

  wire or_1_z0, or_1_z1, or_1_z2, or_1_z3, or_1_z4, or_1_z5, or_1_z6, or_1_z7;

  \or  or_1 (
    .xo(x0), .y0(y0), .x1(x1), .y1(y1), .x2(x2), .y2(y2), .x3(x3), .y3(y3), .x4(x4), .y4(y4), .x5(x5),
    .y5(y5), .x6(x6), .y6(y6), .x7(x7), .y7(y7), .z0(or_1_z0), .z1(or_1_z1), .z2(or_1_z2), .z3(or_1_z3),
    .z4(or_1_z4), .z5(or_1_z5), .z6(or_1_z6), .z7(or_1_z7));
  assign z0 = in_16 ? or_1_z0 : 1'bz;  // Controlled_Buffer controlled_buffer_1
  assign z1 = in_16 ? or_1_z1 : 1'bz;  // Controlled_Buffer controlled_buffer_2
  assign z2 = in_16 ? or_1_z2 : 1'bz;  // Controlled_Buffer controlled_buffer_3
  assign z3 = in_16 ? or_1_z3 : 1'bz;  // Controlled_Buffer controlled_buffer_4
  assign z4 = in_16 ? or_1_z4 : 1'bz;  // Controlled_Buffer controlled_buffer_5
  assign z5 = in_16 ? or_1_z5 : 1'bz;  // Controlled_Buffer controlled_buffer_6
  assign z6 = in_16 ? or_1_z6 : 1'bz;  // Controlled_Buffer controlled_buffer_7
  assign z7 = in_16 ? or_1_z7 : 1'bz;  // Controlled_Buffer controlled_buffer_8
endmodule

module xorwithtri (
  input  x0,
  input  y0,
  input  x1,
  input  y1,
  input  x2,
  input  y2,
  input  x3,
  input  y3,
  input  x4,
  input  y4,
  input  x5,
  input  y5,
  input  x6,
  input  y6,
  input  x7,
  input  in_16,
  input  y7,
  output z0,
  output z1,
  output z2,
  output z3,
  output z4,
  output z5,
  output z6,
  output z7
);

  wire xor_1_z0, xor_1_z1, xor_1_z2, xor_1_z3, xor_1_z4, xor_1_z5, xor_1_z6, xor_1_z7;

  \xor  xor_1 (
    .xo(x0), .y0(y0), .x1(x1), .y1(y1), .x2(x2), .y2(y2), .x3(x3), .y3(y3), .x4(x4), .y4(y4), .x5(x5),
    .y5(y5), .x6(x6), .y6(y6), .x7(x7), .y7(y7), .z0(xor_1_z0), .z1(xor_1_z1), .z2(xor_1_z2), .z3(xor_1_z3),
    .z4(xor_1_z4), .z5(xor_1_z5), .z6(xor_1_z6), .z7(xor_1_z7));
  assign z0 = in_16 ? xor_1_z0 : 1'bz;  // Controlled_Buffer controlled_buffer_1
  assign z1 = in_16 ? xor_1_z1 : 1'bz;  // Controlled_Buffer controlled_buffer_2
  assign z2 = in_16 ? xor_1_z2 : 1'bz;  // Controlled_Buffer controlled_buffer_3
  assign z3 = in_16 ? xor_1_z3 : 1'bz;  // Controlled_Buffer controlled_buffer_4
  assign z4 = in_16 ? xor_1_z4 : 1'bz;  // Controlled_Buffer controlled_buffer_5
  assign z5 = in_16 ? xor_1_z5 : 1'bz;  // Controlled_Buffer controlled_buffer_6
  assign z6 = in_16 ? xor_1_z6 : 1'bz;  // Controlled_Buffer controlled_buffer_7
  assign z7 = in_16 ? xor_1_z7 : 1'bz;  // Controlled_Buffer controlled_buffer_8
endmodule

module notwithtri (
  input  x0,
  input  x1,
  input  x2,
  input  x3,
  input  x4,
  input  x5,
  input  x6,
  input  x7,
  input  in_9,
  output z0,
  output z1,
  output z2,
  output z3,
  output z4,
  output z5,
  output z6,
  output z7
);

  wire not_1_z0, not_1_z1, not_1_z2, not_1_z3, not_1_z4, not_1_z5, not_1_z6, not_1_z7;

  \not  not_1 (
    .xo(x0), .x1(x1), .x2(x2), .x3(x3), .x4(x4), .x5(x5), .x6(x6), .x7(x7), .z0(not_1_z0), .z1(not_1_z1),
    .z2(not_1_z2), .z3(not_1_z3), .z4(not_1_z4), .z5(not_1_z5), .z6(not_1_z6), .z7(not_1_z7));
  assign z0 = in_9 ? not_1_z0 : 1'bz;  // Controlled_Buffer controlled_buffer_1
  assign z1 = in_9 ? not_1_z1 : 1'bz;  // Controlled_Buffer controlled_buffer_2
  assign z2 = in_9 ? not_1_z2 : 1'bz;  // Controlled_Buffer controlled_buffer_3
  assign z3 = in_9 ? not_1_z3 : 1'bz;  // Controlled_Buffer controlled_buffer_4
  assign z4 = in_9 ? not_1_z4 : 1'bz;  // Controlled_Buffer controlled_buffer_5
  assign z5 = in_9 ? not_1_z5 : 1'bz;  // Controlled_Buffer controlled_buffer_6
  assign z6 = in_9 ? not_1_z6 : 1'bz;  // Controlled_Buffer controlled_buffer_7
  assign z7 = in_9 ? not_1_z7 : 1'bz;  // Controlled_Buffer controlled_buffer_8
endmodule
