// Logisim project question6.circ as structural Verilog: 2 circuits, main circuit main
module main (
  input  x0,
  input  x1,
  input  x2,
  input  x3,
  input  s1,
  input  s0,
  output out_7,
  output y2,
  output y1,
  output y0
);

  wire decoder_1_d0, decoder_1_d1, decoder_1_d2, decoder_1_d3;

  decoder decoder_1 (.s1(s1), .s0(s0), .d3(decoder_1_d3), .d2(decoder_1_d2), .d1(decoder_1_d1), .d0(decoder_1_d0));
  assign out_7 = decoder_1_d3 ? x0 : 1'bz;  // Controlled_Buffer controlled_buffer_1
  assign y2 = decoder_1_d2 ? x0 : 1'bz;  // Controlled_Buffer controlled_buffer_2
  assign y1 = decoder_1_d1 ? x0 : 1'bz;  // Controlled_Buffer controlled_buffer_3
  assign y0 = decoder_1_d0 ? x0 : 1'bz;  // Controlled_Buffer controlled_buffer_4
  assign out_7 = decoder_1_d2 ? x1 : 1'bz;  // Controlled_Buffer controlled_buffer_5
  assign y2 = decoder_1_d1 ? x1 : 1'bz;  // Controlled_Buffer controlled_buffer_6
  assign y1 = decoder_1_d0 ? x1 : 1'bz;  // Controlled_Buffer controlled_buffer_7
  assign y0 = decoder_1_d3 ? x1 : 1'bz;  // Controlled_Buffer controlled_buffer_8
  assign out_7 = decoder_1_d1 ? x2 : 1'bz;  // Controlled_Buffer controlled_buffer_9
  assign y2 = decoder_1_d0 ? x2 : 1'bz;  // Controlled_Buffer controlled_buffer_10
  assign y1 = decoder_1_d3 ? x2 : 1'bz;  // Controlled_Buffer controlled_buffer_11
  assign y0 = decoder_1_d2 ? x2 : 1'bz;  // Controlled_Buffer controlled_buffer_12
  assign out_7 = decoder_1_d0 ? x3 : 1'bz;  // Controlled_Buffer controlled_buffer_13
  assign y2 = decoder_1_d3 ? x3 : 1'bz;  // Controlled_Buffer controlled_buffer_14
  assign y1 = decoder_1_d2 ? x3 : 1'bz;  // Controlled_Buffer controlled_buffer_15
  assign y0 = decoder_1_d1 ? x3 : 1'bz;  // Controlled_Buffer controlled_buffer_16

  // Notes on the sheet:
  //   4 bit barrel shifter
endmodule

module decoder (
  input  s1,
  input  s0,
  output d3,
  output d2,
  output d1,
  output d0
);

  wire not_1_out, not_2_out;

  not not_1 (not_1_out, s1);
  not not_2 (not_2_out, s0);
  and and_1 (d3, s1, s0);
  and and_2 (d2, not_1_out, s0);
  and and_3 (d1, s1, not_2_out);
  and and_4 (d0, not_1_out, not_2_out);

  // Notes on the sheet:
  //   2 4 decoder
endmodule
